# Fritzing sketch doktorslab_master (saved by Fritzing 0.9.3b)

parts:
  부품1 = Arduino Uno (Rev3)
  부품2 = NRF24L01+ Breakout Board
  C1 = Electrolytic Capacitor [capacitance=100µF voltage=63V package="100 mil [THT, electrolytic]"]
  BAT1 = BC9VPC [package=bc9vpc]
  부품3 = NRF24L01+ Breakout Board
  부품4 = Bluetooth HC-06
  부품5 = Bluetooth HC-06

nets:
  N1: 부품1.D8, 부품3.CS
  N2: 부품1.D9_PWM, 부품2.CE
  N3: 부품1.D10_PWM/SS, 부품2.CS
  N4: 부품1.D11_PWM/MOSI, 부품2.MOSI, 부품3.MOSI
  N5: 부품1.D12/MISO, 부품2.MISO, 부품3.MISO
  N6: 부품1.D13/SCK, 부품2.SCK, 부품3.SCK
  GND: 부품1.GND, 부품2.GND, C1.-, BAT1.V-, 부품3.GND, 부품4.GND, 부품5.GND
  N7: 부품1.D3_PWM, 부품5.RXD
  N8: 부품1.D4, 부품5.TXD
  N9: 부품1.D5_PWM, 부품4.RXD
  N10: 부품1.D6_PWM, 부품4.TXD
  N11: 부품1.D7, 부품3.CE
  VCC: 부품1.3V3, 부품2.VCC, C1.+, 부품3.VCC
  VCC_2: 부품1.5V, 부품4.VCC, 부품5.VCC
  N12: 부품1.VIN, BAT1.V+
