# Fritzing sketch doktorslab_slave (saved by Fritzing 0.9.3b)

parts:
  부품1 = Arduino Uno (Rev3)
  부품2 = NRF24L01+ Breakout Board
  C1 = Electrolytic Capacitor [capacitance=100µF voltage=63V package="100 mil [THT, electrolytic]"]
  BAT1 = BC9VPC [package=bc9vpc]
  R1 = Resistor [tolerance=±5% resistance=100k package=THT]
  S2 = Pushbutton [package="[THT]"]
  R2 = Resistor [tolerance=±5% resistance=100k package=THT]
  R3 = Resistor [tolerance=±5% resistance=100k package=THT]
  S3 = Pushbutton [package="[THT]"]
  S1 = Pushbutton [package="[THT]"]

nets:
  N1: 부품1.D9_PWM, 부품2.CE
  N2: 부품1.D10_PWM/SS, 부품2.CS
  N3: 부품1.D11_PWM/MOSI, 부품2.MOSI
  N4: 부품1.D12/MISO, 부품2.MISO
  N5: 부품1.D13/SCK, 부품2.SCK
  GND: 부품1.GND, 부품2.GND, BAT1.V-, R1.Pin_0, R2.Pin_0, R3.Pin_0
  N6: 부품1.D2, R3.Pin_1, S3.Pin_3, S3.Pin_4
  N7: 부품1.D3_PWM, S2.Pin_3, S2.Pin_4, R2.Pin_1
  N8: 부품1.D4, R1.Pin_1, S1.Pin_3, S1.Pin_4
  N9: 부품1.3V3, C1.+
  N10: 부품1.5V, S2.Pin_1, S2.Pin_2, S3.Pin_1, S3.Pin_2, S1.Pin_1, S1.Pin_2
  N11: 부품1.VIN, BAT1.V+
  N12: 부품2.VCC, C1.-
